# Fritzing sketch Elektrisch schema (saved by Fritzing 0.9.3b)
breadboards: 1

parts:
  Onderdeel2 = RFID-RC522-v2
  Keypad4x1 = Keypad Membran 4x4
  Onderdeel3 = Arduino Mega 2560 (Rev3)

nets:
  N1: Onderdeel2.SDA, Onderdeel3.D10_PWM
  N2: Onderdeel2.SCK, Onderdeel3.D13_PWM
  N3: Onderdeel2.MISO, Onderdeel3.D12_PWM
  N4: Onderdeel2.IRQ, Onderdeel3.D11_PWM
  GND: Onderdeel2.GND, Onderdeel3.GND
  N5: Onderdeel2.RST, Onderdeel3.D9_PWM
  3.3V: Onderdeel2.3.3V, Onderdeel3.5V
  N6: Keypad4x1.Pin1, Onderdeel3.D23
  N7: Keypad4x1.Pin2, Onderdeel3.D25
  N8: Keypad4x1.Pin3, Onderdeel3.D27
  N9: Keypad4x1.Pin4, Onderdeel3.D29
  N10: Keypad4x1.Pin5, Onderdeel3.D31
  N11: Keypad4x1.Pin6, Onderdeel3.D33
  N12: Keypad4x1.Pin7, Onderdeel3.D35
  N13: Keypad4x1.Pin8, Onderdeel3.D37

custom parts:
  RFID-RC522-v2: A simple China made RFID-RC522 Reader; do check the pin labels, as this is a MFRC522 based clone.
  Keypad Membran 4x4: Membrane Keypad 4x4 Matrix
