# Fritzing sketch motoren (saved by Fritzing 0.9.3b)
breadboards: 1

parts:
  IC1 = L293D [package=THT]
  IC2 = L293D [package=THT]
  M1 = DC Motor
  M2 = DC Motor
  M3 = DC Motor
  M4 = DC Motor  # not connected
  Onderdeel1 = RFID-RC522-v2
  Matrix_keypad1 = KEYPAD 4x4  # not connected
  U1 = ESP32S-HiLetgo [part_number=ESP32S-HiLetgo]

nets:
  N1: IC1.Enable_1, IC1.+Vmotor, IC1.Enable_2, IC1.+V, IC2.Enable_1, IC2.+Vmotor, IC2.Enable_2, IC2.+V, U1.VIN
  GND: IC1.0V, IC2.0V, Onderdeel1.GND, U1.GND
  N2: IC1.Out_3_(_Controlled_by_Enable_2_), M3.pin_2
  N3: IC1.Out_4_(_Controlled_by_Enable_2_), M3.pin_1
  N4: IC2.Out_1_(_Controlled_by_Enable_1_), M1.pin_2
  N5: IC2.Out_2_(_Controlled_by_Enable_1_), M1.pin_1
  N6: IC2.Out_3_(_Controlled_by_Enable_2_), M2.pin_2
  N7: IC2.Out_4_(_Controlled_by_Enable_2_), M2.pin_1
  N8: Onderdeel1.3.3V, U1.3.3

notes:
  Bon printer

custom parts:
  RFID-RC522-v2: A simple China made RFID-RC522 Reader; do check the pin labels, as this is a MFRC522 based clone.
  KEYPAD 4x4: Matrix keypad 16 buttons, 4 rows x 4 columns
  ESP32S-HiLetgo: HiLetgo ESP-WROOM-32 ESP32 ESP-32S Development Board 2.4GHz Dual-Mode WiFi + Bluetooth Dual Cores Microcontroller The ESP32 integrated with Antenna switches, RF Balun, power amplifiers, low-noise amplifiers, filters, and management modules, and the entire solution occupies the least area of PCB. 2.4 GHz Wi-Fi plus Bluetooth dual-mode chip, with TSMC Ultra-low power consumption 40nm technology,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
