# Fritzing sketch motoren (saved by Fritzing 0.9.3b)
breadboards: 1

parts:
  IC1 = L293D [package=THT]
  IC2 = L293D [package=THT]
  M1 = DC Motor
  M2 = DC Motor
  M3 = DC Motor
  M4 = DC Motor  # not connected
  Onderdeel1 = RFID-RC522-v2
  Matrix_keypad1 = KEYPAD 4x4
  U1 = ESP32S-HiLetgo [part_number=ESP32S-HiLetgo]

nets:
  N1: IC1.Enable_1, IC1.+Vmotor, IC1.Enable_2, IC1.+V, IC2.Enable_1, IC2.+Vmotor, IC2.Enable_2, IC2.+V, U1.VIN
  N2: IC1.In_1, U1.GPIO26
  GND: IC1.0V, IC2.0V, Onderdeel1.GND, U1.GND
  N3: IC1.In_2, U1.GPIO27
  N4: IC1.Out_3_(_Controlled_by_Enable_2_), M3.pin_2, U1.GPIO12
  N5: IC1.Out_4_(_Controlled_by_Enable_2_), M3.pin_1
  N6: IC1.In_4, U1.GPIO2
  N7: IC2.In_1, U1.GPIO32
  N8: IC2.Out_1_(_Controlled_by_Enable_1_), M1.pin_2
  N9: IC2.Out_2_(_Controlled_by_Enable_1_), M1.pin_1
  N10: IC2.In_2, U1.GPIO33
  N11: IC2.In_3, U1.GPIO25
  N12: IC2.Out_3_(_Controlled_by_Enable_2_), M2.pin_2
  N13: IC2.Out_4_(_Controlled_by_Enable_2_), M2.pin_1
  N14: IC2.In_4, U1.GPIO15
  N15: Onderdeel1.SDA, U1.GPIO18
  N16: Onderdeel1.SCK, U1.GPIO19
  N17: Onderdeel1.MOSI, U1.GPIO21
  N18: Onderdeel1.MISO, Matrix_keypad1.col2, U1.GPIO22
  N19: Onderdeel1.RST, U1.GPIO23
  N20: Onderdeel1.3.3V, U1.3.3
  N21: Matrix_keypad1.col1, U1.GPIO3
  N22: Matrix_keypad1.col3, U1.GPIO13
  N23: Matrix_keypad1.col4, U1.GPIO17
  N24: Matrix_keypad1.row1, U1.GPIO16
  N25: Matrix_keypad1.row2, U1.GPIO5
  N26: Matrix_keypad1.row3, U1.GPIO4
  N27: Matrix_keypad1.row4, U1.GPIO0

notes:
  Bon printer

custom parts:
  RFID-RC522-v2: A simple China made RFID-RC522 Reader; do check the pin labels, as this is a MFRC522 based clone.
  KEYPAD 4x4: Matrix keypad 16 buttons, 4 rows x 4 columns
  ESP32S-HiLetgo: HiLetgo ESP-WROOM-32 ESP32 ESP-32S Development Board 2.4GHz Dual-Mode WiFi + Bluetooth Dual Cores Microcontroller The ESP32 integrated with Antenna switches, RF Balun, power amplifiers, low-noise amplifiers, filters, and management modules, and the entire solution occupies the least area of PCB. 2.4 GHz Wi-Fi plus Bluetooth dual-mode chip, with TSMC Ultra-low power consumption 40nm technology,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
